// Logisim project feed_the_dot.circ as structural Verilog: 14 circuits, main circuit FEED_THE_DOT (MAIN)
// GPU
module GRAPHIC_PROCESS_UNIT__GPU (
  input  [3:0] in_1,
  input  [3:0] in_2,
  input  clk_in,
  output [15:0] out_4,
  output [15:0] out_5,
  output [15:0] out_6,
  output [15:0] out_7,
  output [15:0] out_8,
  output [15:0] out_9,
  output [15:0] out_10,
  output [15:0] out_11,
  output [15:0] out_12,
  output [15:0] out_13,
  output [15:0] out_14,
  output [15:0] out_15,
  output [15:0] out_16,
  output [15:0] out_17,
  output [15:0] out_18,
  output [15:0] out_19,
  output [3:0] display_show,
  output out_21,
  output clk_changed
);

  wire comparator_1_eq, comparator_2_eq, undriven;
  wire [2:0] adder_1_out, pontuado;
  wire [3:0] adder_2_out, random_1_out, random_2_out;
  wire [15:0] _0, _1, _2, _3, _4, _5, _6, _7, _8, _9, a, b, c, d, demultiplexer_1_out15,
       demultiplexer_3_out15, demultiplexer_4_out0, demultiplexer_4_out1, demultiplexer_4_out2,
       demultiplexer_4_out3, demultiplexer_4_out4, demultiplexer_4_out5, demultiplexer_4_out6,
       demultiplexer_4_out7, demultiplexer_4_out8, demultiplexer_4_out9, demultiplexer_4_out10,
       demultiplexer_4_out11, demultiplexer_4_out12, demultiplexer_4_out13, demultiplexer_4_out14,
       demultiplexer_4_out15, e, f;

  assign out_4 = demultiplexer_4_out0 | _0;  // OR_Gate or_1, 16 bits wide
  Demultiplexer #(.select(4), .enable("false")) demultiplexer_1 (
    .out0(demultiplexer_1_out15[15]), .out1(demultiplexer_1_out15[14]), .out2(demultiplexer_1_out15[13]),
    .out3(demultiplexer_1_out15[12]), .out4(demultiplexer_1_out15[11]), .out5(demultiplexer_1_out15[10]),
    .out6(demultiplexer_1_out15[9]), .out7(demultiplexer_1_out15[8]), .out8(demultiplexer_1_out15[7]),
    .out9(demultiplexer_1_out15[6]), .out10(demultiplexer_1_out15[5]), .out11(demultiplexer_1_out15[4]),
    .out12(demultiplexer_1_out15[3]), .out13(demultiplexer_1_out15[2]), .out14(demultiplexer_1_out15[1]),
    .out15(demultiplexer_1_out15[0]), .sel(random_1_out));  // open: in
  Random #(.width(4)) random_1 (.clk(out_21), .out(random_1_out));  // open: next, clr
  Register #(.width(3), .Select("low")) register_1 (.D(adder_1_out), .Q(pontuado), .clk(out_21));  // open: en, clr
  assign out_5 = demultiplexer_4_out1 | _1;  // OR_Gate or_2, 16 bits wide
  Adder #(.width(3)) adder_1 (.a(pontuado), .b(3'b001), .out(adder_1_out));  // open: cin, cout
  assign out_6 = demultiplexer_4_out2 | _2;  // OR_Gate or_3, 16 bits wide
  Demultiplexer #(.select(4), .width(16), .enable("false")) demultiplexer_2 (
    .out0(_0), .out1(_1), .out2(_2), .out3(_3), .out4(_4), .out5(_5), .out6(_6), .out7(_7), .out8(_8),
    .out9(_9), .out10(a), .out11(b), .out12(c), .out13(d), .out14(e), .out15(f), .in(demultiplexer_1_out15),
    .sel(random_2_out));
  Random #(.width(4)) random_2 (.clk(out_21), .out(random_2_out), .clr(undriven));  // open: next
  assign out_7 = demultiplexer_4_out3 | _3;  // OR_Gate or_4, 16 bits wide
  assign out_8 = demultiplexer_4_out4 | _4;  // OR_Gate or_5, 16 bits wide
  clk_change clk_change_1 (.clk_in(clk_in), .in_2(pontuado), .clk_out(clk_changed));
  assign out_9 = demultiplexer_4_out5 | _5;  // OR_Gate or_6, 16 bits wide
  Demultiplexer #(.select(4), .enable("false")) demultiplexer_3 (
    .out0(demultiplexer_3_out15[15]), .out1(demultiplexer_3_out15[14]), .out2(demultiplexer_3_out15[13]),
    .out3(demultiplexer_3_out15[12]), .out4(demultiplexer_3_out15[11]), .out5(demultiplexer_3_out15[10]),
    .out6(demultiplexer_3_out15[9]), .out7(demultiplexer_3_out15[8]), .out8(demultiplexer_3_out15[7]),
    .out9(demultiplexer_3_out15[6]), .out10(demultiplexer_3_out15[5]), .out11(demultiplexer_3_out15[4]),
    .out12(demultiplexer_3_out15[3]), .out13(demultiplexer_3_out15[2]), .out14(demultiplexer_3_out15[1]),
    .out15(demultiplexer_3_out15[0]), .in(1'b1), .sel(in_2));
  Comparator #(.width(4)) comparator_1 (.a(in_2), .b(random_1_out), .eq(comparator_1_eq));  // open: gt, lt
  Comparator #(.width(4)) comparator_2 (.a(in_1), .b(random_2_out), .eq(comparator_2_eq));  // open: gt, lt
  assign out_10 = demultiplexer_4_out6 | _6;  // OR_Gate or_7, 16 bits wide
  and and_1 (out_21, comparator_1_eq, comparator_2_eq);
  assign out_11 = demultiplexer_4_out7 | _7;  // OR_Gate or_8, 16 bits wide
  Demultiplexer #(.select(4), .width(16), .enable("false")) demultiplexer_4 (
    .out0(demultiplexer_4_out0), .out1(demultiplexer_4_out1), .out2(demultiplexer_4_out2),
    .out3(demultiplexer_4_out3), .out4(demultiplexer_4_out4), .out5(demultiplexer_4_out5),
    .out6(demultiplexer_4_out6), .out7(demultiplexer_4_out7), .out8(demultiplexer_4_out8),
    .out9(demultiplexer_4_out9), .out10(demultiplexer_4_out10), .out11(demultiplexer_4_out11),
    .out12(demultiplexer_4_out12), .out13(demultiplexer_4_out13), .out14(demultiplexer_4_out14),
    .out15(demultiplexer_4_out15), .in(demultiplexer_3_out15), .sel(in_1));
  assign out_12 = demultiplexer_4_out8 | _8;  // OR_Gate or_9, 16 bits wide
  assign out_13 = demultiplexer_4_out9 | _9;  // OR_Gate or_10, 16 bits wide
  assign out_14 = demultiplexer_4_out10 | a;  // OR_Gate or_11, 16 bits wide
  Register #(.width(4), .Select("low")) register_2 (.D(adder_2_out), .Q(display_show), .clk(out_21));  // open: en, clr
  assign out_15 = demultiplexer_4_out11 | b;  // OR_Gate or_12, 16 bits wide
  Adder #(.width(4)) adder_2 (.a(display_show), .b(4'b0001), .out(adder_2_out));  // open: cin, cout
  assign out_16 = demultiplexer_4_out12 | c;  // OR_Gate or_13, 16 bits wide
  assign out_17 = demultiplexer_4_out13 | d;  // OR_Gate or_14, 16 bits wide
  assign out_18 = demultiplexer_4_out14 | e;  // OR_Gate or_15, 16 bits wide
  assign out_19 = demultiplexer_4_out15 | f;  // OR_Gate or_16, 16 bits wide

  // Other names for the same wires on the sheet: display_pt[3:0] = display_show; PONTUACION = out_21

  // Notes on the sheet:
  //   COLUNA 0
  //   COLUNA 1
  //   COLUNA 2
  //   COLUNA 3
  //   COLUNA 4
  //   COLUNA 5
  //   COLUNA 6
  //   COLUNA 7
  //   COLUNA 8
  //   COLUNA 9
  //   COLUNA 1O
  //   COLUNA 11
  //   COLUNA 12
  //   COLUNA 13
  //   COLUNA 14
  //   COLUNA 15
endmodule

module COD (
  input  in_1,
  input  CIMA_BAIXO,
  input  DIREITA_ESQUERDA,
  input  \DIREÇÃO ,
  output [3:0] out_5,
  output [3:0] out_6
);

  wire not_1_out;
  wire [3:0] adder_1_out, adder_2_out, multiplexer_1_out, multiplexer_2_out;

  Multiplexer #(.width(4), .enable("false")) multiplexer_1 (
    .in0(4'b1111), .in1(4'b0001), .out(multiplexer_1_out), .sel(CIMA_BAIXO));
  Multiplexer #(.width(4), .enable("false")) multiplexer_2 (
    .in0(4'b1111), .in1(4'b0001), .out(multiplexer_2_out), .sel(DIREITA_ESQUERDA));
  Adder #(.width(4)) adder_1 (.a(out_5), .b(multiplexer_1_out), .out(adder_1_out));  // open: cin, cout
  Register #(.width(4), .Select("low")) register_1 (
    .D(adder_1_out), .en(not_1_out), .Q(out_5), .clk(in_1));  // open: clr
  not not_1 (not_1_out, \DIREÇÃO );
  Register #(.width(4), .Select("low")) register_2 (
    .D(adder_2_out), .en(\DIREÇÃO ), .Q(out_6), .clk(in_1));  // open: clr
  Adder #(.width(4)) adder_2 (.a(out_6), .b(multiplexer_2_out), .out(adder_2_out));  // open: cin, cout

  // Other names for the same wires on the sheet: cl = in_1

  // Notes on the sheet:
  //   Y
  //   x
  //   1 - mexe no eixo x$0 - mexe no eixo y
endmodule

module FEED_THE_DOT__MAIN (
);

  wire clk_64, clk_plus, tunnel, tunnel_t, tunnel_t_t, tunnel_t_t_t;
  wire [3:0] controller_1_out_6, controller_1_out_7, pts, relogio_e_pts_1_dezena, relogio_e_pts_1_dezena_2,
       relogio_e_pts_1_unidade, relogio_e_pts_1_unidade_2;
  wire [15:0] graphic_process_unit_gpu_1_out_4, graphic_process_unit_gpu_1_out_5,
       graphic_process_unit_gpu_1_out_6, graphic_process_unit_gpu_1_out_7, graphic_process_unit_gpu_1_out_8,
       graphic_process_unit_gpu_1_out_9, graphic_process_unit_gpu_1_out_10,
       graphic_process_unit_gpu_1_out_11, graphic_process_unit_gpu_1_out_12,
       graphic_process_unit_gpu_1_out_13, graphic_process_unit_gpu_1_out_14,
       graphic_process_unit_gpu_1_out_15, graphic_process_unit_gpu_1_out_16,
       graphic_process_unit_gpu_1_out_17, graphic_process_unit_gpu_1_out_18,
       graphic_process_unit_gpu_1_out_19;

  Clock clock_1 (.out(clk_64));
  Button button_1 (.out(tunnel));
  Button button_2 (.out(tunnel_t));
  Button button_3 (.out(tunnel_t_t_t));
  Button button_4 (.out(tunnel_t_t));
  DotMatrix #(.matrixcols(16), .matrixrows(16)) dotmatrix_1 (
    .col0(graphic_process_unit_gpu_1_out_4), .col1(graphic_process_unit_gpu_1_out_5),
    .col2(graphic_process_unit_gpu_1_out_6), .col3(graphic_process_unit_gpu_1_out_7),
    .col4(graphic_process_unit_gpu_1_out_8), .col5(graphic_process_unit_gpu_1_out_9),
    .col6(graphic_process_unit_gpu_1_out_10), .col7(graphic_process_unit_gpu_1_out_11),
    .col8(graphic_process_unit_gpu_1_out_12), .col9(graphic_process_unit_gpu_1_out_13),
    .col10(graphic_process_unit_gpu_1_out_14), .col11(graphic_process_unit_gpu_1_out_15),
    .col12(graphic_process_unit_gpu_1_out_16), .col13(graphic_process_unit_gpu_1_out_17),
    .col14(graphic_process_unit_gpu_1_out_18), .col15(graphic_process_unit_gpu_1_out_19));
  CONTROLLER controller_1 (
    .out_6(controller_1_out_6), .out_7(controller_1_out_7), .Direita(tunnel_t_t_t), .Esquerda(tunnel),
    .Baixo(tunnel_t_t), .Cima(tunnel_t), .in_1(clk_plus));
  GRAPHIC_PROCESS_UNIT__GPU graphic_process_unit_gpu_1 (
    .display_show(pts), .out_4(graphic_process_unit_gpu_1_out_4), .out_5(graphic_process_unit_gpu_1_out_5),
    .out_6(graphic_process_unit_gpu_1_out_6), .out_7(graphic_process_unit_gpu_1_out_7),
    .out_8(graphic_process_unit_gpu_1_out_8), .out_9(graphic_process_unit_gpu_1_out_9),
    .out_10(graphic_process_unit_gpu_1_out_10), .out_11(graphic_process_unit_gpu_1_out_11),
    .out_12(graphic_process_unit_gpu_1_out_12), .out_13(graphic_process_unit_gpu_1_out_13),
    .out_14(graphic_process_unit_gpu_1_out_14), .out_15(graphic_process_unit_gpu_1_out_15),
    .out_16(graphic_process_unit_gpu_1_out_16), .out_17(graphic_process_unit_gpu_1_out_17),
    .out_18(graphic_process_unit_gpu_1_out_18), .out_19(graphic_process_unit_gpu_1_out_19),
    .in_2(controller_1_out_6), .in_1(controller_1_out_7), .clk_changed(clk_plus), .clk_in(clk_64));  // open: out_21
  Hex_Digit_Display hex_digit_display_1 (.value(relogio_e_pts_1_dezena_2));  // open: dp
  RELOGIO_E_PTS relogio_e_pts_1 (
    .Dezena_2(relogio_e_pts_1_dezena_2), .Unidade_2(relogio_e_pts_1_unidade_2),
    .Dezena(relogio_e_pts_1_dezena), .Unidade(relogio_e_pts_1_unidade), .in_1(pts));
  LED led_1 ();  // open: in
  LED led_2 ();  // open: in
  Hex_Digit_Display hex_digit_display_2 (.value(relogio_e_pts_1_unidade_2));  // open: dp
  Hex_Digit_Display hex_digit_display_3 (.value(relogio_e_pts_1_dezena));  // open: dp
  Hex_Digit_Display hex_digit_display_4 (.value(relogio_e_pts_1_unidade));  // open: dp
  Hex_Digit_Display hex_digit_display_5 (.value(pts));  // open: dp

  // Notes on the sheet:
  //   y
  //   X
  //   PLACAR
endmodule

module TEST_MOVE_DOT_01_CIRCUITO_EDUCACIONAL (
  input  CIMA_BAIXO
);

  wire cl;
  wire [3:0] adder_1_out, multiplexer_1_out, register_1_q, register_2_q;
  wire [15:0] graphic_process_unit_gpu_1_p3, graphic_process_unit_gpu_1_p4, graphic_process_unit_gpu_1_p5,
       graphic_process_unit_gpu_1_p6, undriven, undriven_2, undriven_3, undriven_4, undriven_5, undriven_6,
       undriven_7, undriven_8, undriven_9, undriven_10, undriven_11, undriven_12;

  Clock clock_1 (.out(cl));
  Multiplexer #(.width(4), .enable("false")) multiplexer_1 (
    .in0(4'b1111), .in1(4'b0001), .out(multiplexer_1_out), .sel(CIMA_BAIXO));
  Adder #(.width(4)) adder_1 (.a(register_1_q), .b(multiplexer_1_out), .out(adder_1_out));  // open: cin, cout
  Register #(.width(4), .Select("low")) register_1 (.D(adder_1_out), .Q(register_1_q), .clk(cl));  // open: en, clr
  Register #(.width(4), .Select("low")) register_2 (.Q(register_2_q), .clk(cl));  // open: D, en, clr
  DotMatrix #(.matrixcols(16), .matrixrows(16)) dotmatrix_1 (
    .col0(graphic_process_unit_gpu_1_p3), .col1(graphic_process_unit_gpu_1_p4),
    .col2(graphic_process_unit_gpu_1_p5), .col3(graphic_process_unit_gpu_1_p6), .col4(undriven),
    .col5(undriven_2), .col6(undriven_3), .col7(undriven_4), .col8(undriven_5), .col9(undriven_6),
    .col10(undriven_7), .col11(undriven_8), .col12(undriven_9), .col13(undriven_10), .col14(undriven_11),
    .col15(undriven_12));
  // GRAPHIC_PROCESS_UNIT__GPU graphic_process_unit_gpu_1: pin names not known; wires that end beside it: register_1_q, register_1_q, graphic_process_unit_gpu_1_p3, graphic_process_unit_gpu_1_p4, graphic_process_unit_gpu_1_p5, graphic_process_unit_gpu_1_p6

  // Notes on the sheet:
  //   O funcionamento, ainda que primitivo do circuito se baseia no seguinte:$$Temos o registrador que sempre altera o valor vigente de acordo com o 'D', dai $o somador sempre incrementa 1 nesse nosso 'D' resultando no aumento de casas $percorridas pelo nosso dot, até que resete.$$Por outro lado ao colocarmos o MUX na entrada de c-out, o que estamos basicamente $fazendo é escolhendo se queremos somar 1 em 'y'ou diminuir 1 em 'y', isso resulta em$move-lo para cima ou mover para baixo.
endmodule

module TEST_MOVE_DOT_02__CIRCUITO_EDUCACIONAL (
  input  CIMA_BAIXO,
  input  DIREITA_ESQUERDA,
  input  \DIREÇÃO 
);

  wire cl, not_1_out;
  wire [3:0] adder_1_out, adder_2_out, multiplexer_1_out, multiplexer_2_out, register_1_q, register_2_q;
  wire [15:0] graphic_process_unit_gpu_1_p3, graphic_process_unit_gpu_1_p4, graphic_process_unit_gpu_1_p5,
       graphic_process_unit_gpu_1_p6, undriven, undriven_2, undriven_3, undriven_4, undriven_5, undriven_6,
       undriven_7, undriven_8, undriven_9, undriven_10, undriven_11, undriven_12;

  Clock clock_1 (.out(cl));
  Multiplexer #(.width(4), .enable("false")) multiplexer_1 (
    .in0(4'b1111), .in1(4'b0001), .out(multiplexer_1_out), .sel(CIMA_BAIXO));
  Multiplexer #(.width(4), .enable("false")) multiplexer_2 (
    .in0(4'b1111), .in1(4'b0001), .out(multiplexer_2_out), .sel(DIREITA_ESQUERDA));
  Adder #(.width(4)) adder_1 (.a(register_1_q), .b(multiplexer_1_out), .out(adder_1_out));  // open: cin, cout
  Register #(.width(4), .Select("low")) register_1 (
    .D(adder_1_out), .en(\DIREÇÃO ), .Q(register_1_q), .clk(cl));  // open: clr
  Adder #(.width(4)) adder_2 (.a(register_2_q), .b(multiplexer_2_out), .out(adder_2_out));  // open: cin, cout
  Register #(.width(4), .Select("low")) register_2 (
    .D(adder_2_out), .en(not_1_out), .Q(register_2_q), .clk(cl));  // open: clr
  not not_1 (not_1_out, \DIREÇÃO );
  DotMatrix #(.matrixcols(16), .matrixrows(16)) dotmatrix_1 (
    .col0(graphic_process_unit_gpu_1_p3), .col1(graphic_process_unit_gpu_1_p4),
    .col2(graphic_process_unit_gpu_1_p5), .col3(graphic_process_unit_gpu_1_p6), .col4(undriven),
    .col5(undriven_2), .col6(undriven_3), .col7(undriven_4), .col8(undriven_5), .col9(undriven_6),
    .col10(undriven_7), .col11(undriven_8), .col12(undriven_9), .col13(undriven_10), .col14(undriven_11),
    .col15(undriven_12));
  // GRAPHIC_PROCESS_UNIT__GPU graphic_process_unit_gpu_1: pin names not known; wires that end beside it: register_2_q, register_1_q, graphic_process_unit_gpu_1_p3, graphic_process_unit_gpu_1_p4, graphic_process_unit_gpu_1_p5, graphic_process_unit_gpu_1_p6

  // Notes on the sheet:
  //   O funcionamento, ainda que primitivo do circuito se baseia no seguinte:$$Anteriormente conseguimos mover o dot para cima e para baixo por meio $do somador(explicado em test_move_dot 01)$$A logica para mover para os lados direito e esquerdo é semelhante.Comecemos expandindo$o seguinte, adicionemos um mux abaixo que recebe as mesmas entradas que o do eixo y.$Assim teremos controle sobre a direções cima/baixoesquerda e direita. PARA tanto, $conectamos a saida do mux em c-out responsavel por dimensionar 'x.'$$Mas encontramos um problema... ele vai mexer para frente ou para tras ao mesmo tempo$que vai mexer para cima e para baixo, resultando em um efeito diagonal, para driblar isso,$implementamos mais uma entrada que nos dira qual direção estamos tomando como referencia$Exemplo: Quero mexer na direçao de 'x', logo preciso desativar y? faz sentindo ? sim! para isso$ligamos a entrada de direção em y e ligamos de forma negada em 'x'.$$Com isso conseguimos manipular as direçoes, ainda que de forma extramente manual.
endmodule

module TEST_MOVE_DOT03__CIRCUITO_EDUCACIONAL (
  input  DIREITA,
  input  ESQUERDA,
  input  BAIXO,
  input  CIMA
);

  wire clk, conv_for_dot03_circuito_educacional_1_cima_baixo,
       \conv_for_dot03_circuito_educacional_1_direção ,
       conv_for_dot03_circuito_educacional_1_esquerda_direita;
  wire [3:0] cod_1_out_5, cod_1_out_6;
  wire [15:0] graphic_process_unit_gpu_1_p1, graphic_process_unit_gpu_1_p2, graphic_process_unit_gpu_1_p3,
       graphic_process_unit_gpu_1_p4, undriven, undriven_2, undriven_3, undriven_4, undriven_5, undriven_6,
       undriven_7, undriven_8, undriven_9, undriven_10, undriven_11, undriven_12;

  COD cod_1 (
    .CIMA_BAIXO(conv_for_dot03_circuito_educacional_1_cima_baixo),
    .DIREITA_ESQUERDA(conv_for_dot03_circuito_educacional_1_esquerda_direita),
    .\DIREÇÃO (\conv_for_dot03_circuito_educacional_1_direção ), .out_5(cod_1_out_5), .out_6(cod_1_out_6),
    .in_1(clk));
  DotMatrix #(.matrixcols(16), .matrixrows(16)) dotmatrix_1 (
    .col0(graphic_process_unit_gpu_1_p1), .col1(graphic_process_unit_gpu_1_p2),
    .col2(graphic_process_unit_gpu_1_p3), .col3(graphic_process_unit_gpu_1_p4), .col4(undriven),
    .col5(undriven_2), .col6(undriven_3), .col7(undriven_4), .col8(undriven_5), .col9(undriven_6),
    .col10(undriven_7), .col11(undriven_8), .col12(undriven_9), .col13(undriven_10), .col14(undriven_11),
    .col15(undriven_12));
  // GRAPHIC_PROCESS_UNIT__GPU graphic_process_unit_gpu_1: pin names not known; wires that end beside it: graphic_process_unit_gpu_1_p1, graphic_process_unit_gpu_1_p2, graphic_process_unit_gpu_1_p3, graphic_process_unit_gpu_1_p4
  Clock clock_1 (.out(clk));
  CONV_FOR_DOT03__CIRCUITO_EDUCACIONAL conv_for_dot03_circuito_educacional_1 (
    .CIMA_BAIXO(conv_for_dot03_circuito_educacional_1_cima_baixo),
    .ESQUERDA_DIREITA(conv_for_dot03_circuito_educacional_1_esquerda_direita),
    .\DIREÇÃO (\conv_for_dot03_circuito_educacional_1_direção ), .CIMA(CIMA), .BAIXO(BAIXO),
    .ESQUERDA(ESQUERDA), .DIREITA(DIREITA));

  // Notes on the sheet:
  //   y
  //   X
  //   Do test_move_dot03 para este aqui ha um pequeno salto de logica, mas irei explicar da melhor forma que puder.$A começar pelo circuito anterior que fizemos, ele era bom, so que ele nos limitava, para rotacionar o dot, era necessario$sempre mexer na sua direcao, e isso é muito chato, por isso faremos o "CONV" um conversor que ira coletar essas 3 saidas e $modifica-la para 4 entradas(As nossas entradas CIMA, BAIXO, ESQUERDA, DIREITA) nos isentando de  modificar sempre $"direction".$$Sua logica esta no conv_for_dot03
endmodule

// CONV
module CONV_FOR_DOT03__CIRCUITO_EDUCACIONAL (
  input  CIMA,
  input  BAIXO,
  input  ESQUERDA,
  input  DIREITA,
  output CIMA_BAIXO,
  output ESQUERDA_DIREITA,
  output \DIREÇÃO 
);

  wire not_1_out, not_2_out;

  not not_1 (not_1_out, CIMA);
  not not_2 (not_2_out, ESQUERDA);
  and and_1 (CIMA_BAIXO, not_1_out, BAIXO);
  and and_2 (ESQUERDA_DIREITA, not_2_out, DIREITA);
  or or_1 (\DIREÇÃO , ESQUERDA, DIREITA);

  // Notes on the sheet:
  //   0 - CIMA$1- BAIXO$$0 - ESQUERDA$1 - DIREITA$$1 - X$0 - Y
endmodule

module PLAY_MEMORY__CIRCUITO_EDUCACIONAL (
  input  in_1,
  input  in_2,
  input  in_3,
  input  in_4,
  output DIREITA,
  output ESQUERDA,
  output BAIXO,
  output CIMA
);

  wire clk, or_1_out, or_2_out, or_3_out, or_4_out;

  D_Flip_Flop d_ff_1 (.clk(clk), .Q(DIREITA), .preset(in_1), .reset(or_1_out));  // open: D, Qn
  or or_1 (or_1_out, in_2, in_3, in_4);
  D_Flip_Flop d_ff_2 (.clk(clk), .Q(ESQUERDA), .preset(in_2), .reset(or_2_out));  // open: D, Qn
  or or_2 (or_2_out, in_1, in_3, in_4);
  D_Flip_Flop d_ff_3 (.clk(clk), .Q(BAIXO), .preset(in_3), .reset(or_3_out));  // open: D, Qn
  or or_3 (or_3_out, in_1, in_2, in_4);
  Clock clock_1 (.out(clk));
  D_Flip_Flop d_ff_4 (.clk(clk), .Q(CIMA), .preset(in_4), .reset(or_4_out));  // open: D, Qn
  or or_4 (or_4_out, in_1, in_2, in_3);
endmodule

module CONTROLLER (
  input  in_1,
  input  Direita,
  input  Esquerda,
  input  Baixo,
  input  Cima,
  output [3:0] out_6,
  output [3:0] out_7
);

  wire conv_for_dot03_circuito_educacional_1_cima_baixo, \conv_for_dot03_circuito_educacional_1_direção ,
       conv_for_dot03_circuito_educacional_1_esquerda_direita, play_memory_1_baixo, play_memory_1_cima,
       play_memory_1_direita, play_memory_1_esquerda;

  COD cod_1 (
    .CIMA_BAIXO(conv_for_dot03_circuito_educacional_1_cima_baixo),
    .DIREITA_ESQUERDA(conv_for_dot03_circuito_educacional_1_esquerda_direita),
    .\DIREÇÃO (\conv_for_dot03_circuito_educacional_1_direção ), .out_5(out_6), .out_6(out_7), .in_1(in_1));
  PLAY_MEMORY play_memory_1 (
    .DIREITA(play_memory_1_direita), .ESQUERDA(play_memory_1_esquerda), .BAIXO(play_memory_1_baixo),
    .CIMA(play_memory_1_cima), .in_2(Direita), .in_3(Esquerda), .in_4(Baixo), .in_5(Cima), .in_1(in_1));
  CONV_FOR_DOT03__CIRCUITO_EDUCACIONAL conv_for_dot03_circuito_educacional_1 (
    .CIMA_BAIXO(conv_for_dot03_circuito_educacional_1_cima_baixo),
    .ESQUERDA_DIREITA(conv_for_dot03_circuito_educacional_1_esquerda_direita),
    .\DIREÇÃO (\conv_for_dot03_circuito_educacional_1_direção ), .CIMA(play_memory_1_cima),
    .BAIXO(play_memory_1_baixo), .ESQUERDA(play_memory_1_esquerda), .DIREITA(play_memory_1_direita));

  // Other names for the same wires on the sheet: clk = in_1

  // Notes on the sheet:
  //   y
  //   X
endmodule

// MEMORY
module PLAY_MEMORY (
  input  in_1,
  input  in_2,
  input  in_3,
  input  in_4,
  input  in_5,
  output DIREITA,
  output ESQUERDA,
  output BAIXO,
  output CIMA
);

  wire or_1_out, or_2_out, or_3_out, or_4_out;

  D_Flip_Flop d_ff_1 (.clk(in_1), .Q(DIREITA), .preset(in_2), .reset(or_1_out));  // open: D, Qn
  or or_1 (or_1_out, in_3, in_4, in_5);
  D_Flip_Flop d_ff_2 (.clk(in_1), .Q(ESQUERDA), .preset(in_3), .reset(or_2_out));  // open: D, Qn
  or or_2 (or_2_out, in_2, in_4, in_5);
  D_Flip_Flop d_ff_3 (.clk(in_1), .Q(BAIXO), .preset(in_4), .reset(or_3_out));  // open: D, Qn
  or or_3 (or_3_out, in_2, in_3, in_5);
  D_Flip_Flop d_ff_4 (.clk(in_1), .Q(CIMA), .preset(in_5), .reset(or_4_out));  // open: D, Qn
  or or_4 (or_4_out, in_2, in_3, in_4);

  // Other names for the same wires on the sheet: clk = in_1
endmodule

// CRONOMETRO
module RELOGIO_E_PTS (
  input  [3:0] in_1,
  output [3:0] Dezena,
  output [3:0] Unidade,
  output [3:0] Dezena_2,
  output [3:0] Unidade_2
);

  wire _0a59_2_clk_seguinte, clk_out, j_k_ff_1_q, j_k_ff_2_q, j_k_ff_3_q, j_k_ff_4_q, j_k_ff_5_q,
       multiplexer_1_out;

  Clock clk (.out(clk_out));
  Hex_Digit_Display hex_digit_display_1 (.value(Dezena_2));  // open: dp
  J_K_Flip_Flop j_k_ff_1 (.J(1'b1), .clk(clk_out), .K(1'b1), .Q(j_k_ff_1_q));  // open: Qn, preset, reset
  cont_0a59 _0a59 (.Dezena(Dezena_2), .Unidade(Unidade_2), .CLK(_0a59_2_clk_seguinte));  // open: CLK_seguinte, Reset
  Hex_Digit_Display hex_digit_display_2 (.value(Unidade_2));  // open: dp
  J_K_Flip_Flop j_k_ff_2 (.J(1'b1), .clk(j_k_ff_1_q), .K(1'b1), .Q(j_k_ff_2_q));  // open: Qn, preset, reset
  Multiplexer #(.select(4), .enable("false")) multiplexer_1 (
    .in0(j_k_ff_5_q), .in1(j_k_ff_5_q), .in2(j_k_ff_5_q), .in3(j_k_ff_5_q), .in4(j_k_ff_5_q),
    .out(multiplexer_1_out), .sel(in_1));  // open: in5, in6, in7, in8, in9, in10, in11, in12, in13, in14, in15
  Hex_Digit_Display hex_digit_display_3 (.value(Dezena));  // open: dp
  J_K_Flip_Flop j_k_ff_3 (.J(1'b1), .clk(j_k_ff_2_q), .K(1'b1), .Q(j_k_ff_3_q));  // open: Qn, preset, reset
  cont_0a59 _0a59_2 (
    .CLK_seguinte(_0a59_2_clk_seguinte), .Dezena(Dezena), .Unidade(Unidade), .CLK(multiplexer_1_out));  // open: Reset
  Hex_Digit_Display hex_digit_display_4 (.value(Unidade));  // open: dp
  J_K_Flip_Flop j_k_ff_4 (.J(1'b1), .clk(j_k_ff_3_q), .K(1'b1), .Q(j_k_ff_4_q));  // open: Qn, preset, reset
  J_K_Flip_Flop j_k_ff_5 (.J(1'b1), .clk(j_k_ff_4_q), .K(1'b1), .Q(j_k_ff_5_q));  // open: Qn, preset, reset
endmodule

module cont_0a9 (
  input  CLK,
  input  Reset,
  output [3:0] out_3,
  output CLK_seguinte
);

  wire OR_out;
  wire [3:0] adder_1_out;

  Register #(.width(4), .Select("low")) register_1 (.D(adder_1_out), .Q(out_3), .clk(CLK), .clr(OR_out));  // open: en
  Hex_Digit_Display hex_digit_display_1 (.value(out_3));  // open: dp
  or OR (OR_out, CLK_seguinte, Reset);
  Adder #(.width(4)) adder_1 (.a(out_3), .b(4'b0001), .out(adder_1_out));  // open: cin, cout
  nor nor_1 (CLK_seguinte, out_3[0], ~out_3[1], out_3[2], ~out_3[3]);  // NOR_Gate
endmodule

module cont_0a59 (
  input  CLK,
  input  Reset,
  output [3:0] Dezena,
  output [3:0] Unidade,
  output CLK_seguinte
);

  wire _0a9_2_clk_seguinte, OR_out;

  Hex_Digit_Display hex_digit_display_1 (.value(Dezena));  // open: dp
  cont_0a9 _0a9 (.CLK(_0a9_2_clk_seguinte), .Reset(OR_out), .out_3(Dezena));  // open: CLK_seguinte
  nor NOR (CLK_seguinte, Dezena[3], ~Dezena[2], ~Dezena[1], Dezena[0], Unidade[3], Unidade[2], Unidade[1], Unidade[0]);  // NOR_Gate
  Hex_Digit_Display hex_digit_display_2 (.value(Unidade));  // open: dp
  cont_0a9 _0a9_2 (.CLK(CLK), .Reset(OR_out), .out_3(Unidade), .CLK_seguinte(_0a9_2_clk_seguinte));
  or OR (OR_out, CLK_seguinte, Reset);
endmodule

module clk_change (
  input  clk_in,
  input  [2:0] in_2,
  output clk_out
);

  wire j_k_ff_1_q, j_k_ff_2_q, j_k_ff_3_q, j_k_ff_4_q, j_k_ff_5_q;

  J_K_Flip_Flop j_k_ff_1 (.J(1'b1), .clk(clk_in), .K(1'b1), .Q(j_k_ff_1_q));  // open: Qn, preset, reset
  J_K_Flip_Flop j_k_ff_2 (.J(1'b1), .clk(j_k_ff_1_q), .K(1'b1), .Q(j_k_ff_2_q));  // open: Qn, preset, reset
  Multiplexer #(.select(3), .enable("false")) multiplexer_1 (
    .in0(j_k_ff_5_q), .in1(j_k_ff_3_q), .in2(j_k_ff_2_q), .in3(j_k_ff_1_q), .in4(clk_in), .out(clk_out),
    .sel(in_2));  // open: in5, in6, in7
  J_K_Flip_Flop j_k_ff_3 (.J(1'b1), .clk(j_k_ff_2_q), .K(1'b1), .Q(j_k_ff_3_q));  // open: Qn, preset, reset
  J_K_Flip_Flop j_k_ff_4 (.J(1'b1), .clk(j_k_ff_3_q), .K(1'b1), .Q(j_k_ff_4_q));  // open: Qn, preset, reset
  J_K_Flip_Flop j_k_ff_5 (.J(1'b1), .clk(j_k_ff_4_q), .K(1'b1), .Q(j_k_ff_5_q));  // open: Qn, preset, reset
endmodule
